// Digital circuit diglab_03_03.dig as structural Verilog
module diglab_03_03 (
  input  [3:0] In,
  input  [1:0] Selector,
  output A3,
  output A2,
  output A1,
  output A0,
  output B3,
  output B2,
  output B1,
  output B0,
  output C3,
  output C2,
  output C1,
  output C0,
  output D3,
  output D2,
  output D1,
  output D0,
  output Z3,
  output Z2,
  output Z1,
  output Z0,
  output Z3_2,
  output Z2_2,
  output Z1_2,
  output Z0_2,
  output [3:0] Output
);

  wire and_1_out, and_2_out, and_3_out, and_4_out, and_5_out, and_6_out, and_7_out, and_8_out, and_9_out,
       and_10_out, and_11_out, and_12_out, and_13_out, and_14_out, and_15_out, and_16_out, and_17_out,
       and_18_out, and_19_out, and_20_out, and_21_out, and_22_out, and_23_out, and_24_out, and_25_out,
       and_26_out, and_27_out, and_28_out, and_29_out, and_30_out, and_31_out, and_32_out, and_33_out,
       and_34_out, and_35_out, and_36_out, and_37_out, and_38_out, and_39_out, and_40_out, not_1_out,
       not_2_out, not_3_out, not_4_out, not_5_out, not_6_out, not_8_out, not_9_out, not_10_out, not_11_out,
       not_12_out, not_13_out, not_14_out, not_15_out, not_16_out, not_17_out, not_18_out;

  not not_1 (not_1_out, In[3]);
  not not_2 (not_2_out, In[3]);
  not not_3 (not_3_out, In[2]);
  not not_4 (not_4_out, In[2]);
  not not_5 (not_5_out, In[1]);
  not not_6 (not_6_out, In[1]);
  not not_7 (A0, In[0]);
  not not_8 (not_8_out, In[0]);
  and and_1 (and_1_out, In[2], In[1]);
  and and_2 (and_2_out, In[2], In[0]);
  and and_3 (and_3_out, In[2], not_5_out, A0);
  and and_4 (and_4_out, not_3_out, In[1]);
  and and_5 (and_5_out, not_3_out, In[0]);
  and and_6 (and_6_out, In[1], In[0]);
  and and_7 (and_7_out, not_5_out, A0);
  and and_8 (and_8_out, In[2], not_6_out);
  and and_9 (and_9_out, not_4_out, In[1]);
  and and_10 (and_10_out, In[1], not_8_out);
  and and_11 (and_11_out, not_6_out, In[0]);
  or or_1 (A3, and_1_out, In[3], and_2_out);
  or or_2 (A2, and_3_out, and_4_out, and_5_out);
  or or_3 (A1, and_6_out, and_7_out);
  or or_4 (B2, In[3], In[2]);
  or or_5 (B1, and_8_out, and_9_out);
  or or_6 (B0, and_10_out, and_11_out);
  not not_9 (not_9_out, In[3]);
  not not_10 (not_10_out, In[3]);
  not not_11 (not_11_out, In[2]);
  not not_12 (not_12_out, In[2]);
  not not_13 (not_13_out, In[1]);
  not not_14 (not_14_out, In[1]);
  not not_15 (not_15_out, In[0]);
  not not_16 (not_16_out, In[0]);
  and and_12 (and_12_out, In[2], In[1]);
  and and_13 (and_13_out, In[2], In[0]);
  and and_14 (and_14_out, In[2], In[1]);
  and and_15 (and_15_out, In[2], not_15_out);
  and and_16 (and_16_out, In[2], not_13_out, In[0]);
  and and_17 (and_17_out, not_11_out, In[1]);
  and and_18 (and_18_out, In[2], In[0]);
  and and_19 (and_19_out, In[1], In[0]);
  and and_20 (and_20_out, not_12_out, not_14_out, In[0]);
  and and_21 (and_21_out, In[2], In[1]);
  and and_22 (and_22_out, In[2], not_16_out);
  and and_23 (and_23_out, In[2], not_14_out, In[0]);
  and and_24 (and_24_out, In[1], not_16_out);
  or or_7 (C3, and_12_out, In[3], and_13_out);
  or or_8 (C2, and_14_out, In[3], and_15_out);
  or or_9 (C1, and_16_out, In[3], and_17_out);
  or or_10 (D3, and_18_out, In[3], and_19_out);
  or or_11 (D2, and_20_out, and_21_out, and_22_out);
  or or_12 (D1, and_23_out, In[3], and_24_out);
  not not_17 (not_17_out, Selector[1]);
  not not_18 (not_18_out, Selector[0]);
  and and_25 (and_25_out, not_17_out, not_18_out, A3);
  and and_26 (and_26_out, not_17_out, Selector[0], In[3]);
  and and_27 (and_27_out, Selector[1], not_18_out, C3);
  and and_28 (and_28_out, Selector[1], Selector[0], D3);
  and and_29 (and_29_out, not_17_out, not_18_out, A2);
  and and_30 (and_30_out, not_17_out, Selector[0], B2);
  and and_31 (and_31_out, Selector[1], not_18_out, C2);
  and and_32 (and_32_out, Selector[1], Selector[0], D2);
  and and_33 (and_33_out, not_17_out, not_18_out, A1);
  and and_34 (and_34_out, not_17_out, Selector[0], B1);
  and and_35 (and_35_out, Selector[1], not_18_out, C1);
  and and_36 (and_36_out, Selector[1], Selector[0], D1);
  and and_37 (and_37_out, not_17_out, not_18_out, A0);
  and and_38 (and_38_out, not_17_out, Selector[0], B0);
  and and_39 (and_39_out, Selector[1], not_18_out, In[0]);
  and and_40 (and_40_out, Selector[1], Selector[0], In[0]);
  or or_13 (Output[3], and_25_out, and_26_out, and_27_out, and_28_out);
  or or_14 (Output[2], and_29_out, and_30_out, and_31_out, and_32_out);
  or or_15 (Output[1], and_33_out, and_34_out, and_35_out, and_36_out);
  or or_16 (Output[0], and_37_out, and_38_out, and_39_out, and_40_out);

  assign B3 = In[3];
  assign C0 = In[0];
  assign D0 = In[0];
  assign Z0 = Output[0];
  assign Z0_2 = Output[0];
  assign Z1 = Output[1];
  assign Z1_2 = Output[1];
  assign Z2 = Output[2];
  assign Z2_2 = Output[2];
  assign Z3 = Output[3];
  assign Z3_2 = Output[3];

  // Other names for the same wires on the sheet: X0 = In[0]; X1 = In[1]; X2 = In[2]; X3 = In[3]; S0 = Selector[0];
  //   S1 = Selector[1]
endmodule
