// Digital circuit diglab_08_04.dig as structural Verilog
module diglab_08_04 (
  input  clock,
  input  Clr,
  input  P,
  output Z
);

  wire and_1_out, and_2_out, d_ff_1_q, d_ff_2_nq, not_1_out;

  not not_1 (not_1_out, Clr);
  and and_1 (and_1_out, P, not_1_out);
  D_FF d_ff_1 (.D(and_1_out), .C(clock), .Q(d_ff_1_q));  // open: nQ
  D_FF d_ff_2 (.D(d_ff_1_q), .C(clock), .nQ(d_ff_2_nq));  // open: Q
  and and_2 (and_2_out, d_ff_1_q, d_ff_2_nq);
  D_FF d_ff_3 (.D(and_2_out), .C(clock), .Q(Z));  // open: nQ
endmodule
